// Logisim project gaussianFilter3x3.circ as structural Verilog: 1 circuit, main circuit main
module main (
  input  reset,
  input  [15:0] in_0,
  input  [15:0] in_1,
  input  [15:0] in_2,
  input  [15:0] in_3,
  input  [15:0] in_4,
  input  [15:0] in_5,
  input  [15:0] in_6,
  input  [15:0] in_7,
  input  [15:0] in_8,
  output [15:0] out_val
);

  wire clock_out;
  wire [15:0] adder_1_out, adder_2_out, adder_3_out, adder_4_out, adder_5_out, adder_6_out, adder_7_out,
       adder_8_out, adder_9_out, adder_10_out, adder_11_out, register_1_q, register_2_q, register_3_q,
       register_4_q, register_5_q, register_6_q, register_7_q, register_8_q, register_9_q, shifter_1_out,
       shifter_2_out, shifter_3_out, shifter_4_out, shifter_5_out, shifter_6_out, shifter_7_out,
       shifter_8_out, shifter_9_out, subtractor_1_out, subtractor_2_out, subtractor_3_out, subtractor_4_out;

  Register #(.width(16)) register_1 (.D(in_0), .Q(register_1_q), .clk(clock_out));  // open: en, clr
  Register #(.width(16)) register_2 (.D(in_1), .Q(register_2_q), .clk(clock_out));  // open: en, clr
  Register #(.width(16)) register_3 (.D(in_2), .Q(register_3_q), .clk(clock_out));  // open: en, clr
  Register #(.width(16)) register_4 (.D(in_3), .Q(register_4_q), .clk(clock_out));  // open: en, clr
  Register #(.width(16)) register_5 (.D(in_4), .Q(register_5_q), .clk(clock_out));  // open: en, clr
  Register #(.width(16)) register_6 (.D(in_5), .Q(register_6_q), .clk(clock_out));  // open: en, clr
  Register #(.width(16)) register_7 (.D(in_6), .Q(register_7_q), .clk(clock_out));  // open: en, clr
  Register #(.width(16)) register_8 (.D(in_7), .Q(register_8_q), .clk(clock_out));  // open: en, clr
  Register #(.width(16)) register_9 (.D(in_8), .Q(register_9_q), .clk(clock_out));  // open: en, clr
  Adder #(.width(16)) adder_1 (.a(register_1_q), .b(register_3_q), .out(adder_1_out));  // open: cin, cout
  Adder #(.width(16)) adder_2 (.a(register_2_q), .b(register_4_q), .out(adder_2_out));  // open: cin, cout
  Shifter #(.width(16)) shifter_1 (.in(register_5_q), .\dist (4'b0010), .out(shifter_1_out));
  Subtractor #(.width(16)) subtractor_1 (
    .a(shifter_1_out), .b(register_5_q), .out(subtractor_1_out));  // open: bin, bout
  Adder #(.width(16)) adder_3 (.a(register_6_q), .b(register_8_q), .out(adder_3_out));  // open: cin, cout
  Adder #(.width(16)) adder_4 (.a(register_7_q), .b(register_9_q), .out(adder_4_out));  // open: cin, cout
  Adder #(.width(16)) adder_5 (.a(adder_2_out), .b(adder_3_out), .out(adder_5_out));  // open: cin, cout
  Adder #(.width(16)) adder_6 (.a(adder_1_out), .b(adder_4_out), .out(adder_6_out));  // open: cin, cout
  Shifter #(.width(16)) shifter_2 (.in(adder_5_out), .\dist (4'b0100), .out(shifter_2_out));
  Shifter #(.width(16)) shifter_3 (.in(adder_5_out), .\dist (4'b0100), .out(shifter_3_out));
  Shifter #(.width(16)) shifter_4 (.in(adder_6_out), .\dist (4'b0100), .out(shifter_4_out));
  Subtractor #(.width(16)) subtractor_2 (
    .a(shifter_3_out), .b(adder_5_out), .out(subtractor_2_out));  // open: bin, bout
  Subtractor #(.width(16)) subtractor_3 (
    .a(shifter_4_out), .b(adder_6_out), .out(subtractor_3_out));  // open: bin, bout
  Adder #(.width(16)) adder_7 (.a(shifter_2_out), .b(subtractor_2_out), .out(adder_7_out));  // open: cin, cout
  Shifter #(.width(16)) shifter_5 (.in(subtractor_1_out), .\dist (4'b0011), .out(shifter_5_out));
  Clock clock (.out(clock_out));
  Adder #(.width(16)) adder_8 (.a(adder_7_out), .b(subtractor_3_out), .out(adder_8_out));  // open: cin, cout
  Adder #(.width(16)) adder_9 (.a(adder_8_out), .b(shifter_5_out), .out(adder_9_out));  // open: cin, cout
  Shifter #(.width(16), .shift("lr")) shifter_6 (.in(adder_9_out), .\dist (4'b1011), .out(shifter_6_out));
  Shifter #(.width(16), .shift("lr")) shifter_7 (.in(adder_9_out), .\dist (4'b1110), .out(shifter_7_out));
  Shifter #(.width(16), .shift("lr")) shifter_8 (.in(adder_9_out), .\dist (4'b1000), .out(shifter_8_out));
  Shifter #(.width(16), .shift("lr")) shifter_9 (.in(adder_9_out), .\dist (4'b1001), .out(shifter_9_out));
  Subtractor #(.width(16)) subtractor_4 (
    .a(shifter_6_out), .b(shifter_7_out), .out(subtractor_4_out));  // open: bin, bout
  Adder #(.width(16)) adder_10 (.a(shifter_8_out), .b(shifter_9_out), .out(adder_10_out));  // open: cin, cout
  Adder #(.width(16)) adder_11 (.a(subtractor_4_out), .b(adder_10_out), .out(adder_11_out));  // open: cin, cout
  Register #(.width(16)) out_val_reg (.D(adder_11_out), .Q(out_val), .clk(clock_out));  // open: en, clr

  // Notes on the sheet:
  //   Adder_2
  //   Adder_0
  //   sll_0
  //   sub_0
  //   Adder_1
  //   Adder_3
  //   Adder_4
  //   Adder_5
  //   sll_3
  //   sll_1
  //   sll_2
  //   sub_1
  //   sub_2
  //   sll_4
  //   Adder_6
  //   Adder_7
  //   Adder_8
  //   srl_1
  //   srl_0
  //   srl_2
  //   srl_3
  //   sub_3
  //   Adder_9
  //   Adder_10
endmodule
