// Logisim project gaussianFilter5x5.circ as structural Verilog: 1 circuit, main circuit sll_1
module sll_1 (
  input  [15:0] in_0,
  input  [15:0] in_1,
  input  [15:0] in_2,
  input  [15:0] in_3,
  input  [15:0] in_4,
  input  [15:0] in_5,
  input  [15:0] in_6,
  input  [15:0] in_7,
  input  [15:0] in_8,
  input  [15:0] in_9,
  input  [15:0] in_10,
  input  [15:0] in_11,
  input  [15:0] in_12,
  input  [15:0] in_13,
  input  [15:0] in_14,
  input  [15:0] in_15,
  input  [15:0] in_16,
  input  [15:0] in_17,
  input  [15:0] in_18,
  input  [15:0] in_19,
  input  [15:0] in_20,
  input  [15:0] in_21,
  input  [15:0] in_22,
  input  [15:0] in_23,
  input  [15:0] in_24,
  output [15:0] out_val
);

  wire clock_out;
  wire [15:0] adder_1_out, adder_2_out, adder_3_out, adder_4_out, adder_5_out, adder_6_out, adder_7_out,
       adder_8_out, adder_9_out, adder_10_out, adder_11_out, adder_12_out, adder_13_out, adder_15_out,
       adder_16_out, adder_17_out, adder_18_out, adder_19_out, adder_20_out, adder_21_out, adder_22_out,
       adder_23_out, adder_24_out, adder_25_out, adder_26_out, adder_27_out, adder_28_out, adder_29_out,
       adder_30_out, register_1_q, register_2_q, register_3_q, register_4_q, register_5_q, register_6_q,
       register_7_q, register_8_q, register_9_q, register_10_q, register_11_q, register_12_q, register_13_q,
       register_14_q, register_15_q, register_16_q, register_17_q, register_18_q, register_19_q,
       register_20_q, register_21_q, register_22_q, register_23_q, register_24_q, register_25_q,
       shifter_1_out, shifter_2_out, shifter_3_out, shifter_4_out, shifter_5_out, shifter_6_out,
       shifter_7_out, shifter_8_out, subtractor_1_out;

  Register #(.width(16)) register_1 (.D(in_0), .Q(register_1_q), .clk(clock_out));  // open: en, clr
  Register #(.width(16)) register_2 (.D(in_1), .Q(register_2_q), .clk(clock_out));  // open: en, clr
  Register #(.width(16)) register_3 (.D(in_2), .Q(register_3_q), .clk(clock_out));  // open: en, clr
  Register #(.width(16)) register_4 (.D(in_3), .Q(register_4_q), .clk(clock_out));  // open: en, clr
  Register #(.width(16)) register_5 (.D(in_4), .Q(register_5_q), .clk(clock_out));  // open: en, clr
  Register #(.width(16)) register_6 (.D(in_5), .Q(register_6_q), .clk(clock_out));  // open: en, clr
  Register #(.width(16)) register_7 (.D(in_6), .Q(register_7_q), .clk(clock_out));  // open: en, clr
  Register #(.width(16)) register_8 (.D(in_7), .Q(register_8_q), .clk(clock_out));  // open: en, clr
  Register #(.width(16)) register_9 (.D(in_8), .Q(register_9_q), .clk(clock_out));  // open: en, clr
  Register #(.width(16)) register_10 (.D(in_9), .Q(register_10_q), .clk(clock_out));  // open: en, clr
  Register #(.width(16)) register_11 (.D(in_10), .Q(register_11_q), .clk(clock_out));  // open: en, clr
  Register #(.width(16)) register_12 (.D(in_11), .Q(register_12_q), .clk(clock_out));  // open: en, clr
  Register #(.width(16)) register_13 (.D(in_12), .Q(register_13_q), .clk(clock_out));  // open: en, clr
  Register #(.width(16)) register_14 (.D(in_13), .Q(register_14_q), .clk(clock_out));  // open: en, clr
  Register #(.width(16)) register_15 (.D(in_14), .Q(register_15_q), .clk(clock_out));  // open: en, clr
  Register #(.width(16)) register_16 (.D(in_15), .Q(register_16_q), .clk(clock_out));  // open: en, clr
  Register #(.width(16)) register_17 (.D(in_16), .Q(register_17_q), .clk(clock_out));  // open: en, clr
  Register #(.width(16)) register_18 (.D(in_17), .Q(register_18_q), .clk(clock_out));  // open: en, clr
  Register #(.width(16)) register_19 (.D(in_18), .Q(register_19_q), .clk(clock_out));  // open: en, clr
  Register #(.width(16)) register_20 (.D(in_19), .Q(register_20_q), .clk(clock_out));  // open: en, clr
  Register #(.width(16)) register_21 (.D(in_20), .Q(register_21_q), .clk(clock_out));  // open: en, clr
  Register #(.width(16)) register_22 (.D(in_21), .Q(register_22_q), .clk(clock_out));  // open: en, clr
  Register #(.width(16)) register_23 (.D(in_22), .Q(register_23_q), .clk(clock_out));  // open: en, clr
  Register #(.width(16)) register_24 (.D(in_23), .Q(register_24_q), .clk(clock_out));  // open: en, clr
  Register #(.width(16)) register_25 (.D(in_24), .Q(register_25_q), .clk(clock_out));  // open: en, clr
  Adder #(.width(16)) adder_1 (.a(register_1_q), .b(register_2_q), .out(adder_1_out));  // open: cin, cout
  Adder #(.width(16)) adder_2 (.a(register_3_q), .b(register_4_q), .out(adder_2_out));  // open: cin, cout
  Adder #(.width(16)) adder_3 (.a(register_5_q), .b(register_6_q), .out(adder_3_out));  // open: cin, cout
  Adder #(.width(16)) adder_4 (.a(register_7_q), .b(register_8_q), .out(adder_4_out));  // open: cin, cout
  Shifter #(.width(16)) shifter_1 (.in(register_9_q), .\dist (4'b0100), .out(shifter_1_out));
  Adder #(.width(16)) adder_5 (.a(register_10_q), .b(register_11_q), .out(adder_5_out));  // open: cin, cout
  Adder #(.width(16)) adder_6 (.a(register_12_q), .b(register_13_q), .out(adder_6_out));  // open: cin, cout
  Adder #(.width(16)) adder_7 (.a(register_14_q), .b(register_15_q), .out(adder_7_out));  // open: cin, cout
  Adder #(.width(16)) adder_8 (.a(register_16_q), .b(register_17_q), .out(adder_8_out));  // open: cin, cout
  Adder #(.width(16)) adder_9 (.a(register_18_q), .b(register_19_q), .out(adder_9_out));  // open: cin, cout
  Adder #(.width(16)) adder_10 (.a(register_20_q), .b(register_21_q), .out(adder_10_out));  // open: cin, cout
  Adder #(.width(16)) adder_11 (.a(register_22_q), .b(register_23_q), .out(adder_11_out));  // open: cin, cout
  Adder #(.width(16)) adder_12 (.a(register_24_q), .b(register_25_q), .out(adder_12_out));  // open: cin, cout
  Adder #(.width(16)) adder_13 (.a(adder_1_out), .b(adder_2_out), .out(adder_13_out));  // open: cin, cout
  Adder #(.width(16)) adder_14 (.a(adder_3_out), .b(adder_4_out), .out(adder_13_out));  // open: cin, cout
  Subtractor #(.width(16)) subtractor_1 (
    .a(shifter_1_out), .b(register_9_q), .out(subtractor_1_out));  // open: bin, bout
  Adder #(.width(16)) adder_15 (.a(adder_5_out), .b(adder_6_out), .out(adder_15_out));  // open: cin, cout
  Adder #(.width(16)) adder_16 (.a(adder_7_out), .b(adder_8_out), .out(adder_16_out));  // open: cin, cout
  Adder #(.width(16)) adder_17 (.a(adder_9_out), .b(adder_10_out), .out(adder_17_out));  // open: cin, cout
  Adder #(.width(16)) adder_18 (.a(adder_11_out), .b(adder_12_out), .out(adder_18_out));  // open: cin, cout
  Adder #(.width(16)) adder_19 (.a(adder_13_out), .b(adder_13_out), .out(adder_19_out));  // open: cin, cout
  Adder #(.width(16)) adder_20 (.a(adder_13_out), .b(adder_15_out), .out(adder_20_out));  // open: cin, cout
  Adder #(.width(16)) adder_21 (.a(adder_13_out), .b(adder_15_out), .out(adder_21_out));  // open: cin, cout
  Adder #(.width(16)) adder_22 (.a(adder_16_out), .b(adder_17_out), .out(adder_22_out));  // open: cin, cout
  Shifter #(.width(16)) shifter_2 (.in(adder_18_out), .\dist (4'b0001), .out(shifter_2_out));
  Clock clock (.out(clock_out));
  Adder #(.width(16)) adder_23 (.a(adder_20_out), .b(adder_22_out), .out(adder_23_out));  // open: cin, cout
  Adder #(.width(16)) adder_24 (.a(adder_19_out), .b(shifter_2_out), .out(adder_24_out));  // open: cin, cout
  Shifter #(.width(16)) shifter_3 (.in(adder_21_out), .\dist (4'b0011), .out(shifter_3_out));
  Shifter #(.width(16)) shifter_4 (.in(adder_23_out), .\dist (4'b0010), .out(shifter_4_out));
  Adder #(.width(16)) adder_25 (.a(shifter_3_out), .b(shifter_4_out), .out(adder_25_out));  // open: cin, cout
  Adder #(.width(16)) adder_26 (.a(subtractor_1_out), .b(adder_24_out), .out(adder_26_out));  // open: cin, cout
  Adder #(.width(16)) adder_27 (.a(adder_25_out), .b(adder_26_out), .out(adder_27_out));  // open: cin, cout
  Shifter #(.width(16), .shift("lr")) shifter_5 (.in(adder_27_out), .\dist (4'b1000), .out(shifter_5_out));
  Shifter #(.width(16), .shift("lr")) shifter_6 (.in(adder_27_out), .\dist (4'b1001), .out(shifter_6_out));
  Shifter #(.width(16), .shift("lr")) shifter_7 (.in(adder_27_out), .\dist (4'b1100), .out(shifter_7_out));
  Shifter #(.width(16), .shift("lr")) shifter_8 (.in(adder_27_out), .\dist (4'b1101), .out(shifter_8_out));
  Adder #(.width(16)) adder_28 (.a(shifter_5_out), .b(shifter_6_out), .out(adder_28_out));  // open: cin, cout
  Adder #(.width(16)) adder_29 (.a(shifter_7_out), .b(shifter_8_out), .out(adder_29_out));  // open: cin, cout
  Adder #(.width(16)) adder_30 (.a(adder_28_out), .b(adder_29_out), .out(adder_30_out));  // open: cin, cout
  Register #(.width(16)) out_val_reg (.D(adder_30_out), .Q(out_val), .clk(clock_out));  // open: en, clr

  // Notes on the sheet:
  //   adder_7
  //   adder_8
  //   adder_9
  //   adder_10
  //   sll_0
  //   adder_5
  //   adder_6
  //   adder_3
  //   adder_4
  //   adder_1
  //   adder_2
  //   adder_11
  //   adder_12
  //   sub_1
  //   adder_16
  //   adder_17
  //   adder_15
  //   adder_14
  //   adder_13
  //   adder_18
  //   adder_21
  //   adder_20
  //   adder_22
  //   adder_19
  //   sll_1
  //   adder_23
  //   adder_24
  //   sll_2
  //   sll_3
  //   adder_25
  //   adder_26
  //   adder_27
  //   srl_1
  //   srl_0
  //   srl_2
  //   srl_3
  //   adder_28
  //   adder_29
  //   adder_30
endmodule
