// Logisim project gaussianFilter7x7.circ as structural Verilog: 1 circuit, main circuit adder_9
module adder_9 (
  input  [15:0] in_0,
  input  [15:0] in_1,
  input  [15:0] in_2,
  input  [15:0] in_3,
  input  [15:0] in_4,
  input  [15:0] in_5,
  input  [15:0] in_6,
  input  [15:0] in_7,
  input  [15:0] in_8,
  input  [15:0] in_9,
  input  [15:0] in_10,
  input  [15:0] in_11,
  input  [15:0] in_12,
  input  [15:0] in_13,
  input  [15:0] in_14,
  input  [15:0] in_15,
  input  [15:0] in_16,
  input  [15:0] in_17,
  input  [15:0] in_18,
  input  [15:0] in_19,
  input  [15:0] in_20,
  input  [15:0] in_21,
  input  [15:0] in_22,
  input  [15:0] in_23,
  input  [15:0] in_24,
  input  [15:0] in_25,
  input  [15:0] in_26,
  input  [15:0] in_27,
  input  [15:0] in_28,
  input  [15:0] in_29,
  input  [15:0] in_30,
  input  [15:0] in_31,
  input  [15:0] in_32,
  input  [15:0] in_33,
  input  [15:0] in_34,
  input  [15:0] in_35,
  input  [15:0] in_36,
  input  [15:0] in_37,
  input  [15:0] in_38,
  input  [15:0] in_39,
  input  [15:0] in_40,
  input  [15:0] in_41,
  input  [15:0] in_42,
  input  [15:0] in_43,
  input  [15:0] in_44,
  input  [15:0] in_45,
  input  [15:0] in_46,
  input  [15:0] in_47,
  input  [15:0] in_47_2,
  output [15:0] out_val
);

  wire undriven, undriven_2;
  wire [15:0] adder_1_out, adder_7_out, adder_28_out, adder_29_out, adder_30_out, register_1_q, register_2_q,
       register_3_q, register_4_q, register_5_q, register_6_q, register_7_q, register_8_q, register_9_q,
       register_10_q, register_11_q, register_12_q, register_13_q, register_14_q, register_15_q,
       register_16_q, register_17_q, register_18_q, register_19_q, register_20_q, register_21_q,
       register_22_q, register_23_q, register_24_q, register_25_q, register_26_q, register_27_q,
       register_28_q, register_29_q, register_30_q, register_31_q, register_32_q, register_33_q,
       register_34_q, register_35_q, register_36_q, register_37_q, register_38_q, register_39_q,
       register_40_q, register_41_q, register_42_q, register_43_q, register_44_q, register_45_q,
       register_46_q, register_47_q, register_48_q, register_49_q, shifter_2_out, shifter_3_out,
       shifter_4_out, shifter_5_out, undriven_3, undriven_4, undriven_5, undriven_6, undriven_7, undriven_8,
       undriven_9, undriven_10, undriven_11, undriven_12, undriven_13, undriven_14, undriven_15, undriven_16,
       undriven_17;

  Register #(.width(16)) register_1 (.D(in_0), .Q(register_1_q), .clk(undriven));  // open: en, clr
  Register #(.width(16)) register_2 (.D(in_1), .Q(register_2_q), .clk(undriven));  // open: en, clr
  Register #(.width(16)) register_3 (.D(in_2), .Q(register_3_q), .clk(undriven));  // open: en, clr
  Register #(.width(16)) register_4 (.D(in_3), .Q(register_4_q), .clk(undriven));  // open: en, clr
  Register #(.width(16)) register_5 (.D(in_4), .Q(register_5_q), .clk(undriven));  // open: en, clr
  Register #(.width(16)) register_6 (.D(in_5), .Q(register_6_q), .clk(undriven));  // open: en, clr
  Register #(.width(16)) register_7 (.D(in_6), .Q(register_7_q), .clk(undriven));  // open: en, clr
  Register #(.width(16)) register_8 (.D(in_7), .Q(register_8_q), .clk(undriven));  // open: en, clr
  Register #(.width(16)) register_9 (.D(in_8), .Q(register_9_q), .clk(undriven));  // open: en, clr
  Register #(.width(16)) register_10 (.D(in_9), .Q(register_10_q), .clk(undriven));  // open: en, clr
  Register #(.width(16)) register_11 (.D(in_10), .Q(register_11_q), .clk(undriven));  // open: en, clr
  Register #(.width(16)) register_12 (.D(in_11), .Q(register_12_q), .clk(undriven));  // open: en, clr
  Register #(.width(16)) register_13 (.D(in_12), .Q(register_13_q), .clk(undriven));  // open: en, clr
  Register #(.width(16)) register_14 (.D(in_13), .Q(register_14_q), .clk(undriven));  // open: en, clr
  Register #(.width(16)) register_15 (.D(in_14), .Q(register_15_q), .clk(undriven));  // open: en, clr
  Register #(.width(16)) register_16 (.D(in_15), .Q(register_16_q), .clk(undriven));  // open: en, clr
  Register #(.width(16)) register_17 (.D(in_16), .Q(register_17_q), .clk(undriven));  // open: en, clr
  Register #(.width(16)) register_18 (.D(in_17), .Q(register_18_q), .clk(undriven));  // open: en, clr
  Register #(.width(16)) register_19 (.D(in_18), .Q(register_19_q), .clk(undriven));  // open: en, clr
  Register #(.width(16)) register_20 (.D(in_19), .Q(register_20_q), .clk(undriven));  // open: en, clr
  Register #(.width(16)) register_21 (.D(in_20), .Q(register_21_q), .clk(undriven));  // open: en, clr
  Register #(.width(16)) register_22 (.D(in_21), .Q(register_22_q), .clk(undriven));  // open: en, clr
  Register #(.width(16)) register_23 (.D(in_22), .Q(register_23_q), .clk(undriven));  // open: en, clr
  Register #(.width(16)) register_24 (.D(in_23), .Q(register_24_q), .clk(undriven));  // open: en, clr
  Register #(.width(16)) register_25 (.D(in_24), .Q(register_25_q), .clk(undriven));  // open: en, clr
  Register #(.width(16)) register_26 (.D(in_25), .Q(register_26_q), .clk(undriven_2));  // open: en, clr
  Register #(.width(16)) register_27 (.D(in_26), .Q(register_27_q), .clk(undriven_2));  // open: en, clr
  Register #(.width(16)) register_28 (.D(in_27), .Q(register_28_q), .clk(undriven_2));  // open: en, clr
  Register #(.width(16)) register_29 (.D(in_28), .Q(register_29_q), .clk(undriven_2));  // open: en, clr
  Register #(.width(16)) register_30 (.D(in_29), .Q(register_30_q), .clk(undriven_2));  // open: en, clr
  Register #(.width(16)) register_31 (.D(in_30), .Q(register_31_q), .clk(undriven_2));  // open: en, clr
  Register #(.width(16)) register_32 (.D(in_31), .Q(register_32_q), .clk(undriven_2));  // open: en, clr
  Register #(.width(16)) register_33 (.D(in_32), .Q(register_33_q), .clk(undriven_2));  // open: en, clr
  Register #(.width(16)) register_34 (.D(in_33), .Q(register_34_q), .clk(undriven_2));  // open: en, clr
  Register #(.width(16)) register_35 (.D(in_34), .Q(register_35_q), .clk(undriven_2));  // open: en, clr
  Register #(.width(16)) register_36 (.D(in_35), .Q(register_36_q), .clk(undriven_2));  // open: en, clr
  Register #(.width(16)) register_37 (.D(in_36), .Q(register_37_q), .clk(undriven_2));  // open: en, clr
  Register #(.width(16)) register_38 (.D(in_37), .Q(register_38_q), .clk(undriven_2));  // open: en, clr
  Register #(.width(16)) register_39 (.D(in_38), .Q(register_39_q), .clk(undriven_2));  // open: en, clr
  Register #(.width(16)) register_40 (.D(in_39), .Q(register_40_q), .clk(undriven_2));  // open: en, clr
  Register #(.width(16)) register_41 (.D(in_40), .Q(register_41_q), .clk(undriven_2));  // open: en, clr
  Register #(.width(16)) register_42 (.D(in_41), .Q(register_42_q), .clk(undriven_2));  // open: en, clr
  Register #(.width(16)) register_43 (.D(in_42), .Q(register_43_q), .clk(undriven_2));  // open: en, clr
  Register #(.width(16)) register_44 (.D(in_43), .Q(register_44_q), .clk(undriven_2));  // open: en, clr
  Register #(.width(16)) register_45 (.D(in_44), .Q(register_45_q), .clk(undriven_2));  // open: en, clr
  Register #(.width(16)) register_46 (.D(in_45), .Q(register_46_q), .clk(undriven_2));  // open: en, clr
  Register #(.width(16)) register_47 (.D(in_46), .Q(register_47_q), .clk(undriven_2));  // open: en, clr
  Register #(.width(16)) register_48 (.D(in_47), .Q(register_48_q), .clk(undriven_2));  // open: en, clr
  Register #(.width(16)) register_49 (.D(in_47_2), .Q(register_49_q), .clk(undriven_2));  // open: en, clr
  Adder #(.width(16)) adder_1 (.a(register_31_q), .b(register_33_q), .out(adder_1_out));  // open: cin, cout
  Adder #(.width(16)) adder_2 (.a(register_2_q), .b(register_3_q));  // open: out, cin, cout
  Adder #(.width(16)) adder_3 (.a(register_4_q), .b(register_5_q));  // open: out, cin, cout
  Adder #(.width(16)) adder_4 (.a(register_6_q), .b(register_8_q));  // open: out, cin, cout
  Adder #(.width(16)) adder_5 (.a(register_10_q), .b(register_12_q));  // open: out, cin, cout
  Adder #(.width(16)) adder_6 (.a(register_9_q), .b(register_13_q));  // open: out, cin, cout
  Adder #(.width(16)) adder_7 (.a(register_14_q), .b(register_15_q), .out(adder_7_out));  // open: cin, cout
  Adder #(.width(16)) adder_8 (.a(register_16_q), .b(register_20_q));  // open: out, cin, cout
  Adder #(.width(16)) adder_9 (.a(register_17_q), .b(register_19_q));  // open: out, cin, cout
  Adder #(.width(16)) adder_10 (.a(register_21_q), .b(register_22_q));  // open: out, cin, cout
  Adder #(.width(16)) adder_11 (.a(register_11_q), .b(register_23_q));  // open: out, cin, cout
  Adder #(.width(16)) adder_12 (.a(register_28_q), .b(register_29_q));  // open: out, cin, cout
  Adder #(.width(16)) adder_13 (.a(register_26_q), .b(register_32_q));  // open: out, cin, cout
  Adder #(.width(16)) adder_14 (.a(register_27_q), .b(register_39_q));  // open: out, cin, cout
  Adder #(.width(16)) adder_15 (.a(register_30_q), .b(register_34_q));  // open: out, cin, cout
  Adder #(.width(16)) adder_16 (.a(register_35_q), .b(register_36_q));  // open: out, cin, cout
  Adder #(.width(16)) adder_17 (.a(register_38_q), .b(register_40_q));  // open: out, cin, cout
  Adder #(.width(16)) adder_18 (.a(register_37_q), .b(register_41_q));  // open: out, cin, cout
  Adder #(.width(16)) adder_19 (.a(register_42_q), .b(register_44_q));  // open: out, cin, cout
  Adder #(.width(16)) adder_20 (.a(register_45_q), .b(register_46_q));  // open: out, cin, cout
  Adder #(.width(16)) adder_21 (.a(register_47_q), .b(register_48_q));  // open: out, cin, cout
  Adder #(.width(16)) adder_22 (.a(register_18_q), .b(register_24_q));  // open: out, cin, cout
  Adder #(.width(16)) adder_23 (.a(undriven_3), .b(undriven_4));  // open: out, cin, cout
  Shifter #(.width(16)) shifter_1 (.in(undriven_13), .\dist (4'b0100));  // open: out
  Adder #(.width(16)) adder_24 (.a(undriven_5), .b(undriven_6));  // open: out, cin, cout
  Adder #(.width(16)) adder_25 (.a(undriven_7), .b(undriven_8));  // open: out, cin, cout
  Adder #(.width(16)) adder_26 (.a(undriven_9), .b(undriven_10));  // open: out, cin, cout
  Adder #(.width(16)) adder_27 (.a(undriven_11), .b(undriven_12));  // open: out, cin, cout
  Shifter #(.width(16), .shift("lr")) shifter_2 (.in(undriven_14), .\dist (4'b1000), .out(shifter_2_out));
  Shifter #(.width(16), .shift("lr")) shifter_3 (.in(undriven_15), .\dist (4'b1001), .out(shifter_3_out));
  Shifter #(.width(16), .shift("lr")) shifter_4 (.in(undriven_16), .\dist (4'b1100), .out(shifter_4_out));
  Shifter #(.width(16), .shift("lr")) shifter_5 (.in(undriven_17), .\dist (4'b1101), .out(shifter_5_out));
  Adder #(.width(16)) adder_28 (.a(shifter_2_out), .b(shifter_3_out), .out(adder_28_out));  // open: cin, cout
  Adder #(.width(16)) adder_29 (.a(shifter_4_out), .b(shifter_5_out), .out(adder_29_out));  // open: cin, cout
  Adder #(.width(16)) adder_30 (.a(adder_28_out), .b(adder_29_out), .out(adder_30_out));  // open: cin, cout
  Register #(.width(16)) out_val_reg (.D(adder_30_out), .Q(out_val), .clk(undriven));  // open: en, clr

  // Notes on the sheet:
  //   adder_22
  //   adder_1
  //   adder_2
  //   adder_3
  //   adder_17
  //   adder_13
  //   adder_4
  //   adder_19
  //   adder_21
  //   adder_15
  //   adder_5
  //   adder_11
  //   adder_6
  //   adder_16
  //   adder_12
  //   adder_19
  //   adder_7
  //   adder_20
  //   adder_14
  //   adder_8
  //   adder_7
  //   adder_8
  //   adder_10
  //   adder_1
  //   adder_2
  //   adder_11
  //   adder_12
  //   sll_0
  //   srl_1
  //   srl_0
  //   srl_2
  //   srl_3
  //   adder_28
  //   adder_29
  //   adder_30
endmodule
